# Fritzing sketch lcd_displey_schcema (saved by Fritzing 0.9.3b)
breadboards: 1

parts:
  Súčiastka2 = Arduino Mega 2560 (Rev3)
  U1 = LCD-16X2 [package=lcd-16x2]
  R1 = Rotary Potentiometer (Small) [maximum_resistance=100kΩ package=THT]
  R2 = Resistor [tolerance=±5% resistance=220 package=THT]

nets:
  N1: Súčiastka2.D11_PWM, U1.DB7
  N2: Súčiastka2.D10_PWM, U1.DB6
  N3: Súčiastka2.D9_PWM, U1.DB5
  N4: Súčiastka2.D8_PWM, U1.DB4
  5V: Súčiastka2.5V, U1.VDD, R1.leg1, R2.Pin_1
  GND: Súčiastka2.GND, U1.VSS, U1.R_W, U1.K, R1.leg2
  N5: Súčiastka2.D0_RX0, U1.RS
  N6: Súčiastka2.D1_TX0, U1.E
  N7: U1.VO, R1.wiper
  N8: U1.A, R2.Pin_0

notes:
  I'm useing 10K potenciometer and 220 Ω rezistor.S
